// Logisim project 16_4prencoder.circ as structural Verilog: 1 circuit, main circuit main
module main (
);

  wire dipswitch_1_p1, dipswitch_1_p2, dipswitch_1_p3, dipswitch_1_p4, dipswitch_1_p5, dipswitch_1_p6,
       dipswitch_1_p7;

  // DipSwitch #(.number(16)) dipswitch_1: pin names not known; wires that end beside it: dipswitch_1_p1, dipswitch_1_p2, dipswitch_1_p3, dipswitch_1_p4, dipswitch_1_p5, dipswitch_1_p6, dipswitch_1_p7
  prencoder42 prencoder42_1 (
    .A0(dipswitch_1_p1), .A1(dipswitch_1_p2), .A2(dipswitch_1_p3), .A3(dipswitch_1_p4));  // open: Y0, Y1
  prencoder42 prencoder42_2 (.A1(dipswitch_1_p5), .A2(dipswitch_1_p6), .A3(dipswitch_1_p7));  // open: A0, Y0, Y1
  // prencoder42 prencoder42_3: pin names not known
  // prencoder42 prencoder42_4: pin names not known
endmodule
