// Logisim project 2_4decoder.circ as structural Verilog: 1 circuit, main circuit decoder_2_4
module decoder_2_4 (
  input  in1,
  input  in2,
  output out0,
  output out1,
  output out2,
  output out3
);

  wire not_1_out, not_2_out;

  not not_1 (not_1_out, in1);
  not not_2 (not_2_out, in2);
  and and_1 (out0, not_1_out, not_2_out);
  and and_2 (out1, not_2_out, in1);
  and and_3 (out2, not_1_out, in2);
  and and_4 (out3, in1, in2);
endmodule
