// Logisim project 3_8decoder.circ as structural Verilog: 1 circuit, main circuit main
module main (
  input  in1,
  input  in2,
  input  in3,
  output o0,
  output o1,
  output o2,
  output o3,
  output o4,
  output o5,
  output o6,
  output o7
);

  wire decoder_2_4_1_out0, decoder_2_4_1_out1, decoder_2_4_1_out2, decoder_2_4_1_out3, decoder_2_4_2_out0,
       decoder_2_4_2_out1, decoder_2_4_2_out2, decoder_2_4_2_out3;

  decoder_2_4 decoder_2_4_1 (
    .in1(in1), .in2(in2), .out0(decoder_2_4_1_out0), .out1(decoder_2_4_1_out1), .out2(decoder_2_4_1_out2),
    .out3(decoder_2_4_1_out3));
  decoder_2_4 decoder_2_4_2 (
    .in1(in1), .in2(in2), .out0(decoder_2_4_2_out0), .out1(decoder_2_4_2_out1), .out2(decoder_2_4_2_out2),
    .out3(decoder_2_4_2_out3));
  and and_1 (o0, decoder_2_4_1_out0, ~in3);  // AND_Gate
  and and_2 (o1, decoder_2_4_1_out1, ~in3);  // AND_Gate
  and and_3 (o2, decoder_2_4_1_out2, ~in3);  // AND_Gate
  and and_4 (o3, decoder_2_4_1_out3, ~in3);  // AND_Gate
  and and_5 (o4, in3, decoder_2_4_2_out0);
  and and_6 (o5, in3, decoder_2_4_2_out1);
  and and_7 (o6, in3, decoder_2_4_2_out2);
  and and_8 (o7, in3, decoder_2_4_2_out3);

  // Notes on the sheet:
  //   3
  //   7
endmodule
