// Logisim project 3b4_1selector.circ as structural Verilog: 1 circuit, main circuit main
module main (
  input  in_1,
  input  in_2,
  input  in_3,
  input  in_4,
  input  in_5,
  input  in_6,
  output out_7
);

  wire and_1_out, and_2_out, and_3_out, and_4_out, and_5_out, nor_1_out, nor_2_out, nor_3_out;

  nor nor_1 (nor_1_out, in_3, in_4);
  nor nor_2 (nor_2_out, ~in_3, in_4);  // NOR_Gate
  nor nor_3 (nor_3_out, in_3, ~in_4);  // NOR_Gate
  and and_1 (and_1_out, in_4, in_3);
  and and_2 (and_2_out, in_1, nor_1_out);
  and and_3 (and_3_out, in_2, nor_2_out);
  and and_4 (and_4_out, nor_3_out, in_5);
  and and_5 (and_5_out, and_1_out, in_6);
  or or_1 (out_7, and_2_out, and_3_out, and_4_out, and_5_out);
endmodule
