// Logisim project 4bitadder.circ as structural Verilog: 1 circuit, main circuit main
module main (
  input  in_1,
  input  [3:0] in_2,
  input  [3:0] in_3
);

  wire fa_1_cout, fa_2_cout, fa_3_cout, fa_4_cout;
  wire [3:0] fa_1_s;

  FA fa_1 (.A(in_2[0]), .B(in_3[0]), .Cin(in_1), .S(fa_1_s[0]), .Cout(fa_1_cout));
  Hex_Digit_Display hex_digit_display_1 (.value(in_2));  // open: dp
  FA fa_2 (.A(in_2[1]), .B(in_3[1]), .Cin(fa_1_cout), .S(fa_1_s[1]), .Cout(fa_2_cout));
  FA fa_3 (.A(in_2[2]), .B(in_3[2]), .Cin(fa_2_cout), .S(fa_1_s[2]), .Cout(fa_3_cout));
  FA fa_4 (.A(in_2[3]), .B(in_3[3]), .Cin(fa_3_cout), .S(fa_1_s[3]), .Cout(fa_4_cout));
  Hex_Digit_Display hex_digit_display_2 (.value(in_3));  // open: dp
  LED led_1 (.in(fa_4_cout));
  Hex_Digit_Display hex_digit_display_3 (.value(fa_1_s));  // open: dp

  // Notes on the sheet:
  //   +
  //   =
endmodule
