// Logisim project 7segmentWencoder.circ as structural Verilog: 1 circuit, main circuit main
module main (
);

  wire a_out, b_out, c_out, d_out, decoder_2_4_1_out0, decoder_2_4_1_out1, decoder_2_4_1_out2,
       decoder_2_4_1_out3, decoder_2_4_2_out0, decoder_2_4_2_out1, decoder_2_4_2_out2, decoder_2_4_2_out3,
       decoder_2_4_3_out0, decoder_2_4_3_out1, decoder_2_4_3_out2, decoder_2_4_3_out3, decoder_2_4_4_out0,
       decoder_2_4_4_out1, decoder_2_4_4_out2, decoder_2_4_4_out3, dipswitch_1_p1, dipswitch_1_p2,
       dipswitch_1_p3, dipswitch_1_p4, dipswitch_1_p5, dipswitch_1_p6, dipswitch_1_p7, dipswitch_1_p8,
       dipswitch_1_p9, dipswitch_1_p10, dipswitch_1_p11, dipswitch_1_p12, dipswitch_1_p13, dipswitch_1_p14,
       dipswitch_1_p15, e_out, f_out, g_out, h_out, o0_out, o1_out, o2_out, o3_out, o4_out, o5_out, o6_out,
       o7_out, o8_out, o9_out, o10_out, o11_out, o12_out, o13_out, o14_out, o15_out, or_1_out, or_2_out,
       or_3_out, or_4_out;

  // DipSwitch #(.number(15)) dipswitch_1: pin names not known; wires that end beside it: dipswitch_1_p1, dipswitch_1_p2, dipswitch_1_p3, dipswitch_1_p4, dipswitch_1_p5, dipswitch_1_p6, dipswitch_1_p7, dipswitch_1_p8, dipswitch_1_p9, dipswitch_1_p10, dipswitch_1_p11, dipswitch_1_p12, dipswitch_1_p13, dipswitch_1_p14, dipswitch_1_p15
  or or_1 (or_1_out, dipswitch_1_p1, dipswitch_1_p3, dipswitch_1_p5, dipswitch_1_p7, dipswitch_1_p11, dipswitch_1_p9, dipswitch_1_p13, dipswitch_1_p15);
  or or_2 (or_2_out, dipswitch_1_p2, dipswitch_1_p3, dipswitch_1_p6, dipswitch_1_p7, dipswitch_1_p10, dipswitch_1_p11, dipswitch_1_p14, dipswitch_1_p15);
  or or_3 (or_3_out, dipswitch_1_p15, dipswitch_1_p14, dipswitch_1_p13, dipswitch_1_p12, dipswitch_1_p7, dipswitch_1_p6, dipswitch_1_p5, dipswitch_1_p4);
  or or_4 (or_4_out, dipswitch_1_p15, dipswitch_1_p14, dipswitch_1_p13, dipswitch_1_p12, dipswitch_1_p11, dipswitch_1_p10, dipswitch_1_p9, dipswitch_1_p8);
  decoder_2_4 decoder_2_4_1 (
    .in1(or_1_out), .in2(or_2_out), .out0(decoder_2_4_1_out0), .out1(decoder_2_4_1_out1),
    .out2(decoder_2_4_1_out2), .out3(decoder_2_4_1_out3));
  decoder_2_4 decoder_2_4_2 (
    .in1(or_1_out), .in2(or_2_out), .out0(decoder_2_4_2_out0), .out1(decoder_2_4_2_out1),
    .out2(decoder_2_4_2_out2), .out3(decoder_2_4_2_out3));
  decoder_2_4 decoder_2_4_3 (
    .in1(or_1_out), .in2(or_2_out), .out0(decoder_2_4_3_out0), .out1(decoder_2_4_3_out1),
    .out2(decoder_2_4_3_out2), .out3(decoder_2_4_3_out3));
  decoder_2_4 decoder_2_4_4 (
    .in1(or_1_out), .in2(or_2_out), .out0(decoder_2_4_4_out0), .out1(decoder_2_4_4_out1),
    .out2(decoder_2_4_4_out2), .out3(decoder_2_4_4_out3));
  and o0 (o0_out, decoder_2_4_1_out0, ~or_4_out, ~or_3_out);  // AND_Gate
  and o1 (o1_out, decoder_2_4_1_out1, ~or_4_out, ~or_3_out);  // AND_Gate
  and o2 (o2_out, decoder_2_4_1_out2, ~or_4_out, ~or_3_out);  // AND_Gate
  and o3 (o3_out, decoder_2_4_1_out3, ~or_4_out, ~or_3_out);  // AND_Gate
  and o4 (o4_out, or_3_out, ~or_4_out, decoder_2_4_2_out0);  // AND_Gate
  and o5 (o5_out, or_3_out, ~or_4_out, decoder_2_4_2_out1);  // AND_Gate
  and o6 (o6_out, or_3_out, ~or_4_out, decoder_2_4_2_out2);  // AND_Gate
  and o7 (o7_out, or_3_out, ~or_4_out, decoder_2_4_2_out3);  // AND_Gate
  and o8 (o8_out, decoder_2_4_3_out0, or_4_out, ~or_3_out);  // AND_Gate
  and o9 (o9_out, decoder_2_4_3_out1, or_4_out, ~or_3_out);  // AND_Gate
  and o10 (o10_out, decoder_2_4_3_out2, or_4_out, ~or_3_out);  // AND_Gate
  and o11 (o11_out, decoder_2_4_3_out3, or_4_out, ~or_3_out);  // AND_Gate
  and o12 (o12_out, or_3_out, or_4_out, decoder_2_4_4_out0);
  and o13 (o13_out, or_3_out, or_4_out, decoder_2_4_4_out1);
  and o14 (o14_out, or_3_out, or_4_out, decoder_2_4_4_out2);
  and o15 (o15_out, or_3_out, or_4_out, decoder_2_4_4_out3);
  or a (a_out, o0_out, o2_out, o3_out, o5_out, o6_out, o7_out, o8_out, o9_out);
  or b (b_out, o0_out, o1_out, o2_out, o3_out, o4_out, o7_out, o8_out, o9_out);
  or c (c_out, o0_out, o1_out, o3_out, o4_out, o5_out, o6_out, o7_out, o8_out, o9_out);
  or d (d_out, o2_out, o0_out, o3_out, o5_out, o6_out, o8_out, o9_out);
  or e (e_out, o0_out, o2_out, o6_out, o8_out);
  or f (f_out, o0_out, o4_out, o5_out, o6_out, o8_out, o9_out);
  or g (g_out, o2_out, o3_out, o4_out, o5_out, o6_out, o8_out, o9_out);
  or h (h_out, o10_out, o11_out, o12_out, o14_out, o13_out, o15_out);
  _7_Segment_Display u_7_segment_display_1 (
    .g(g_out), .f(f_out), .a(a_out), .b(b_out), .e(e_out), .d(d_out), .c(c_out), .dp(h_out));

  // Notes on the sheet:
  //   16-4 Encoder
  //   3
  //   7
  //   3
  //   7
  //   4-16 decoder
  //   mapping
endmodule
