// Logisim project DFlipFlop.circ as structural Verilog: 1 circuit, main circuit main
module main (
  input  D,
  input  reset,
  input  in_3,
  input  reset_2,
  output Qslave,
  output master,
  output out_7,
  output out_8
);

  wire clk_out, clock_1_out, not_1_out, not_2_out;

  Clock clk (.out(clk_out));
  Clock clock_1 (.out(clock_1_out));
  not not_1 (not_1_out, clk_out);
  dlatchWrst dlatchwrst_1 (.EN(not_1_out), .clk(reset), .RST(D), .Q(master));  // open: D, Q0
  dlatchWrst dlatchwrst_2 (.EN(clock_1_out), .clk(reset_2), .RST(in_3), .Q(out_8));  // open: D, Q0
  not not_2 (not_2_out, clock_1_out);
  dlatchWrst dlatchwrst_3 (.EN(not_2_out), .RST(out_8), .Q(out_7));  // open: clk, D, Q0
  dlatchWrst dlatchwrst_4 (.EN(clk_out), .RST(master), .Q(Qslave));  // open: clk, D, Q0

  // Notes on the sheet:
  //   falling edge
endmodule
