// Logisim project DLatch.circ as structural Verilog: 1 circuit, main circuit dlatchWrst
module dlatchWrst (
  input  EN,
  input  clk,
  input  RST,
  input  D,
  output Q,
  output Q0
);

  wire and_1_out, and_2_out;

  and and_1 (and_1_out, D, EN, clk);
  and and_2 (and_2_out, clk, ~EN);  // AND_Gate
  nor nor_1 (Q, and_1_out, RST, Q0);
  nor nor_2 (Q0, Q, RST, and_2_out);
endmodule
