// Logisim project 3b4_1selector.circ as structural Verilog: 1 circuit, main circuit main
module main (
  input  [2:0] in_1,
  input  [2:0] in_2,
  input  in_3,
  input  in_4,
  input  [2:0] in_5,
  input  [2:0] in_6,
  output [2:0] out_7
);

  wire [2:0] and_2_out, and_3_out, and_4_out, and_5_out;
  wire [2:2] and_1_out, nor_1_out, nor_2_out, nor_3_out;

  nor nor_1 (nor_1_out[2], in_3, in_4);
  nor nor_2 (nor_2_out[2], ~in_3, in_4);  // NOR_Gate
  nor nor_3 (nor_3_out[2], in_3, ~in_4);  // NOR_Gate
  and and_1 (and_1_out[2], in_4, in_3);
  assign and_2_out = in_1 & {3{nor_1_out[2]}};  // AND_Gate and_2, 3 bits wide
  assign and_3_out = in_2 & {3{nor_2_out[2]}};  // AND_Gate and_3, 3 bits wide
  assign and_4_out = {3{nor_3_out[2]}} & in_5;  // AND_Gate and_4, 3 bits wide
  assign and_5_out = {3{and_1_out[2]}} & in_6;  // AND_Gate and_5, 3 bits wide
  assign out_7 = and_2_out | and_3_out | and_4_out | and_5_out;  // OR_Gate or_1, 3 bits wide
endmodule
