// Logisim project 4_2pr_encoder.circ as structural Verilog: 1 circuit, main circuit prencoder42
module prencoder42 (
  input  A0,
  input  A1,
  input  A2,
  input  A3,
  output Y0,
  output Y1
);

  wire nor_1_out, or_1_out;

  or or_1 (or_1_out, A1, A3);
  or or_2 (Y1, A2, A3);
  nor nor_1 (nor_1_out, ~or_1_out, Y1);  // NOR_Gate
  xor xor_1 (Y0, nor_1_out, A3);
endmodule
