// Logisim project 4bitcounter.circ as structural Verilog: 1 circuit, main circuit main
module main (
  input  [3:0] plus1
);

  wire adder_1_cout, clock_1_out, not_1_out;
  wire [3:0] adder_1_out, dlatchwrst_1_q0;

  Adder #(.width(4)) adder_1 (.a(plus1), .b(dlatchwrst_1_q0), .out(adder_1_out), .cout(adder_1_cout));  // open: cin
  Hex_Digit_Display hex_digit_display_1 (.value(dlatchwrst_1_q0));  // open: dp
  not not_1 (not_1_out, adder_1_cout);
  Clock clock_1 (.out(clock_1_out));
  dlatchWrst dlatchwrst_1 (
    .EN(not_1_out), .clk(clock_1_out), .RST(adder_1_cout), .D(adder_1_out[0]), .Q0(dlatchwrst_1_q0[0]));  // open: Q
  dlatchWrst dlatchwrst_2 (
    .EN(not_1_out), .clk(clock_1_out), .RST(adder_1_cout), .D(adder_1_out[1]), .Q0(dlatchwrst_1_q0[1]));  // open: Q
  dlatchWrst dlatchwrst_3 (
    .EN(not_1_out), .clk(clock_1_out), .RST(adder_1_cout), .D(adder_1_out[2]), .Q0(dlatchwrst_1_q0[2]));  // open: Q
  dlatchWrst dlatchwrst_4 (
    .EN(not_1_out), .clk(clock_1_out), .RST(adder_1_cout), .D(adder_1_out[3]), .Q0(dlatchwrst_1_q0[3]));  // open: Q
endmodule
