// Logisim project 4bitregister.circ as structural Verilog: 1 circuit, main circuit main
module main (
  input  rst,
  input  en
);

  wire clk_out, dipswitch_1_p1, dipswitch_1_p2, dipswitch_1_p3, dipswitch_1_p4;
  wire [3:0] dlatchwrst_1_q0;

  // DipSwitch #(.number(4)) dipswitch_1: pin names not known; wires that end beside it: dipswitch_1_p1, dipswitch_1_p2, dipswitch_1_p3, dipswitch_1_p4
  Clock clk (.out(clk_out));
  dlatchWrst dlatchwrst_1 (.EN(en), .clk(clk_out), .RST(rst), .D(dipswitch_1_p1), .Q0(dlatchwrst_1_q0[0]));  // open: Q
  dlatchWrst dlatchwrst_2 (.EN(en), .clk(clk_out), .RST(rst), .D(dipswitch_1_p2), .Q0(dlatchwrst_1_q0[1]));  // open: Q
  dlatchWrst dlatchwrst_3 (.EN(en), .clk(clk_out), .RST(rst), .D(dipswitch_1_p3), .Q0(dlatchwrst_1_q0[2]));  // open: Q
  dlatchWrst dlatchwrst_4 (.EN(en), .clk(clk_out), .RST(rst), .D(dipswitch_1_p4), .Q0(dlatchwrst_1_q0[3]));  // open: Q
  Hex_Digit_Display hex_digit_display_1 (.value(dlatchwrst_1_q0));  // open: dp
endmodule
