// Logisim project 4bitsignmag_sub.circ as structural Verilog: 1 circuit, main circuit main
module main (
  input  [3:0] in_1,
  input  [3:0] in_2
);

  wire and_1_out, or_1_out, subtractor_1_bout;
  wire [3:0] adder_1_out, multiplexer_1_out, subtractor_1_out;

  Hex_Digit_Display hex_digit_display_1 (.value({1'b0, in_1[2:0]}));  // open: dp
  Adder #(.width(4)) adder_1 (.a({1'b0, in_1[2:0]}), .b({1'b0, in_2[2:0]}), .out(adder_1_out));  // open: cin, cout
  Multiplexer #(.width(4)) multiplexer_1 (
    .in0(adder_1_out), .in1(subtractor_1_out), .out(multiplexer_1_out), .sel(or_1_out));
  or or_1 (or_1_out, in_1[3], in_2[3]);
  Subtractor #(.width(4)) subtractor_1 (
    .a({1'b0, in_1[2:0]}), .b({1'b0, in_2[2:0]}), .out(subtractor_1_out), .bout(subtractor_1_bout));  // open: bin
  Hex_Digit_Display hex_digit_display_2 (.value({1'b0, in_2[2:0]}));  // open: dp
  _7_Segment_Display u_7_segment_display_1 (.g(and_1_out));  // open: f, a, b, e, d, c, dp
  and and_1 (and_1_out, or_1_out, subtractor_1_bout);
  Hex_Digit_Display hex_digit_display_3 (.value(multiplexer_1_out));  // open: dp
endmodule
