// Logisim project 7segwithhexadec.circ as structural Verilog: 1 circuit, main circuit main
module main (
  input  in_1,
  input  in_2,
  input  in_3
);

  wire a_out, and_1_out, and_2_out, b_out, c_out, d_out, decoder_2_4_1_out0, decoder_2_4_1_out1,
       decoder_2_4_1_out2, decoder_2_4_1_out3, decoder_2_4_2_out0, decoder_2_4_2_out1, decoder_2_4_2_out2,
       decoder_2_4_2_out3, decoder_2_4_3_out0, decoder_2_4_3_out1, decoder_2_4_3_out2, decoder_2_4_3_out3,
       decoder_2_4_4_out0, decoder_2_4_4_out1, decoder_2_4_4_out2, decoder_2_4_4_out3, dipswitch_1_sw1,
       dipswitch_1_sw2, dipswitch_1_sw3, dipswitch_1_sw4, dipswitch_1_sw5, e_out, f_out, g_out, not_1_out,
       o0_out, o1_out, o2_out, o3_out, o4_out, o5_out, o6_out, o7_out, o8_out, o10_out, o11_out, o12_out,
       o13_out, o15_out, or_1_out, xor_1_out, xor_2_out, xor_3_out, xor_4_out, xor_5_out, xor_6_out,
       xor_7_out, xor_8_out;

  DipSwitch #(.number(5)) dipswitch_1 (
    .sw1(dipswitch_1_sw1), .sw2(dipswitch_1_sw2), .sw3(dipswitch_1_sw3), .sw4(dipswitch_1_sw4),
    .sw5(dipswitch_1_sw5));
  ExactlyOne xor_1 (.out(xor_1_out), .in0(in_1), .in1(in_2), .in2(in_3));
  decoder_2_4 decoder_2_4_1 (
    .in1(dipswitch_1_sw1), .in2(dipswitch_1_sw2), .out0(decoder_2_4_1_out0), .out1(decoder_2_4_1_out1),
    .out2(decoder_2_4_1_out2), .out3(decoder_2_4_1_out3));
  decoder_2_4 decoder_2_4_2 (
    .in1(dipswitch_1_sw1), .in2(dipswitch_1_sw2), .out0(decoder_2_4_2_out0), .out1(decoder_2_4_2_out1),
    .out2(decoder_2_4_2_out2), .out3(decoder_2_4_2_out3));
  decoder_2_4 decoder_2_4_3 (
    .in1(dipswitch_1_sw1), .in2(dipswitch_1_sw2), .out0(decoder_2_4_3_out0), .out1(decoder_2_4_3_out1),
    .out2(decoder_2_4_3_out2), .out3(decoder_2_4_3_out3));
  decoder_2_4 decoder_2_4_4 (
    .in1(dipswitch_1_sw1), .in2(dipswitch_1_sw2), .out0(decoder_2_4_4_out0), .out1(decoder_2_4_4_out1),
    .out2(decoder_2_4_4_out2), .out3(decoder_2_4_4_out3));
  and o0 (o0_out, decoder_2_4_1_out0, ~dipswitch_1_sw4, ~dipswitch_1_sw3);  // AND_Gate
  and o1 (o1_out, decoder_2_4_1_out1, ~dipswitch_1_sw4, ~dipswitch_1_sw3);  // AND_Gate
  and o2 (o2_out, decoder_2_4_1_out2, ~dipswitch_1_sw4, ~dipswitch_1_sw3);  // AND_Gate
  and o3 (o3_out, decoder_2_4_1_out3, ~dipswitch_1_sw4, ~dipswitch_1_sw3);  // AND_Gate
  and o4 (o4_out, dipswitch_1_sw3, ~dipswitch_1_sw4, decoder_2_4_2_out0);  // AND_Gate
  and o5 (o5_out, dipswitch_1_sw3, ~dipswitch_1_sw4, decoder_2_4_2_out1);  // AND_Gate
  and o6 (o6_out, dipswitch_1_sw3, ~dipswitch_1_sw4, decoder_2_4_2_out2);  // AND_Gate
  and o7 (o7_out, dipswitch_1_sw3, ~dipswitch_1_sw4, decoder_2_4_2_out3);  // AND_Gate
  and o8 (o8_out, decoder_2_4_3_out0, dipswitch_1_sw4, ~dipswitch_1_sw3);  // AND_Gate
  and o9 (o8_out, decoder_2_4_3_out1, dipswitch_1_sw4, ~dipswitch_1_sw3);  // AND_Gate
  and o10 (o10_out, decoder_2_4_3_out2, dipswitch_1_sw4, ~dipswitch_1_sw3);  // AND_Gate
  and o11 (o11_out, decoder_2_4_3_out3, dipswitch_1_sw4, ~dipswitch_1_sw3);  // AND_Gate
  and o12 (o12_out, dipswitch_1_sw3, dipswitch_1_sw4, decoder_2_4_4_out0);
  and o13 (o13_out, dipswitch_1_sw3, dipswitch_1_sw4, decoder_2_4_4_out1);
  and o14 (o6_out, dipswitch_1_sw3, dipswitch_1_sw4, decoder_2_4_4_out2);
  and o15 (o15_out, dipswitch_1_sw3, dipswitch_1_sw4, decoder_2_4_4_out3);
  or or_1 (or_1_out, o15_out, o6_out, o13_out, o12_out, o11_out, o10_out);
  and and_1 (and_1_out, or_1_out, not_1_out);
  not not_1 (not_1_out, dipswitch_1_sw5);
  and and_2 (and_2_out, dipswitch_1_sw5, or_1_out);
  xor xor_2 (xor_2_out, o10_out, and_1_out);
  or a (a_out, o0_out, o2_out, o3_out, o5_out, o6_out, o7_out, o8_out, o8_out, xor_2_out);
  or b (b_out, o0_out, o1_out, o2_out, o3_out, o4_out, o7_out, o8_out, o8_out, xor_3_out);
  xor xor_3 (xor_3_out, and_1_out, o11_out);
  or f (f_out, o0_out, o4_out, o5_out, o6_out, o8_out, o8_out, o2_out, xor_4_out);
  xor xor_4 (xor_4_out, and_1_out, o12_out);
  _7_Segment_Display u_7_segment_display_1 (
    .g(g_out), .f(f_out), .a(a_out), .b(b_out), .e(e_out), .d(d_out), .c(c_out), .dp(and_2_out));
  or g (g_out, o2_out, o3_out, o4_out, o5_out, o6_out, o8_out, o8_out, xor_5_out);
  xor xor_5 (xor_5_out, and_1_out, o13_out);
  or d (d_out, o0_out, o2_out, o3_out, o5_out, o6_out, o8_out, o8_out, xor_6_out);
  xor xor_6 (xor_6_out, and_1_out, o6_out);
  or e (e_out, o0_out, o2_out, o4_out, o6_out, o8_out, xor_7_out);
  xor xor_7 (xor_7_out, and_1_out, o15_out);
  or c (c_out, o0_out, o1_out, o3_out, o4_out, o5_out, o6_out, o7_out, o8_out, o8_out, xor_8_out);
  buf xor_8 (xor_8_out, and_1_out);  // XOR_Gate

  // Notes on the sheet:
  //   need to reroute all this spaghetti: 10-15 to XORs
  //   and negate selector pins of XORs
  //   3
  //   7
  //   3
  //   7
endmodule
