// Logisim project comparator_eq.circ as structural Verilog: 1 circuit, main circuit main
module main (
  input  in_1,
  input  in_2,
  input  in_3,
  input  in_4,
  input  in_5,
  input  in_6,
  input  in_7,
  input  in_8,
  input  [3:0] in_9,
  input  [3:0] in_10,
  output out_11
);

  wire and_2_out, xnor_1_out, xnor_2_out, xnor_3_out, xnor_4_out;
  wire [3:0] xnor_5_out;

  xnor xnor_1 (xnor_1_out, in_1, in_2);
  xnor xnor_2 (xnor_2_out, in_3, in_4);
  xnor xnor_3 (xnor_3_out, in_5, in_6);
  xnor xnor_4 (xnor_4_out, in_7, in_8);
  assign xnor_5_out = ~(in_9 ^ in_10);  // XNOR_Gate xnor_5, 4 bits wide
  and and_1 (out_11, xnor_1_out, xnor_2_out, xnor_3_out, xnor_4_out);
  and and_2 (and_2_out, xnor_5_out[0], xnor_5_out[1], xnor_5_out[2], xnor_5_out[3]);
  LED led_1 (.in(and_2_out));
endmodule
