// Logisim project fulladder.circ as structural Verilog: 2 circuits, main circuit FA
module FA (
  input  A,
  input  B,
  input  Cin,
  output S,
  output Cout
);

  wire and_1_out, and_2_out, xor_1_out;

  xor xor_1 (xor_1_out, A, B);
  and and_1 (and_1_out, A, B);
  xor xor_2 (S, xor_1_out, Cin);
  and and_2 (and_2_out, xor_1_out, Cin);
  or or_1 (Cout, and_2_out, and_1_out);
endmodule

module FA4bit (
  input  [3:0] A,
  input  [3:0] B,
  input  [3:0] Cin,
  output [3:0] S,
  output [3:0] Cout
);

  wire [3:0] and_1_out, and_2_out, xor_1_out;

  assign xor_1_out = A ^ B;  // XOR_Gate xor_1, 4 bits wide
  assign and_1_out = A & B;  // AND_Gate and_1, 4 bits wide
  assign S = xor_1_out ^ Cin;  // XOR_Gate xor_2, 4 bits wide
  assign and_2_out = xor_1_out & Cin;  // AND_Gate and_2, 4 bits wide
  assign Cout = and_2_out | and_1_out;  // OR_Gate or_1, 4 bits wide
endmodule
