// Logisim project xnor_attempts.circ as structural Verilog: 1 circuit, main circuit main
module main (
  input  in_1,
  input  in_2,
  input  in_3,
  output out_4
);

  wire transistor_1_out, transistor_2_out, undriven;

  Transistor transistor_1 (.in(undriven), .out(transistor_1_out), .gate(in_1));
  Transistor #(.\type ("n")) transistor_2 (.in(transistor_1_out), .out(transistor_2_out), .gate(in_1));
  Transistor #(.\type ("n")) transistor_3 (.in(in_2), .out(out_4), .gate(in_1));
  Transistor transistor_4 (.in(in_2), .out(out_4), .gate(transistor_1_out));
  // also tied to GND on the sheet: transistor_2_out

  // Notes on the sheet:
  //   XNOR = (A & B) | (A ~| B)
endmodule
