// Logisim project RAMwithREG.circ as structural Verilog: 1 circuit, main circuit main
module main (
  input  [7:0] in_1,
  input  [1:0] addr,
  input  en,
  input  rst,
  output [7:0] r0val,
  output [7:0] r1val,
  output [7:0] r2val,
  output [7:0] r3val
);

  wire and_1_out, and_2_out, and_3_out, and_4_out, clock_1_out, decoder_1_out0, decoder_1_out1,
       decoder_1_out2, decoder_1_out3;

  Decoder #(.select(2)) decoder_1 (
    .out0(decoder_1_out0), .out1(decoder_1_out1), .out2(decoder_1_out2), .out3(decoder_1_out3), .sel(addr));  // open: en
  Register r0 (.D(in_1), .en(and_1_out), .clk(clock_1_out), .Q(r0val), .clr(rst));
  and and_1 (and_1_out, decoder_1_out0, en);
  Register r1 (.D(in_1), .en(and_2_out), .clk(clock_1_out), .Q(r1val), .clr(rst));
  and and_2 (and_2_out, decoder_1_out1, en);
  Register r2 (.D(in_1), .en(and_3_out), .clk(clock_1_out), .Q(r2val), .clr(rst));
  and and_3 (and_3_out, decoder_1_out2, en);
  Register r3 (.D(in_1), .en(and_4_out), .clk(clock_1_out), .Q(r3val), .clr(rst));
  and and_4 (and_4_out, decoder_1_out3, en);
  Clock clock_1 (.out(clock_1_out));
endmodule
