// Logisim project ROMwithMUX.circ as structural Verilog: 1 circuit, main circuit main
module main (
  input  [7:0] in_1,
  input  [7:0] in_2,
  input  [7:0] in_3,
  input  [7:0] in_4,
  input  [7:0] in_5,
  input  [7:0] in_6,
  input  [7:0] in_7,
  input  [7:0] in_8,
  input  [7:0] unused,
  input  in_10,
  input  [3:0] in_11,
  input  in_12,
  output [7:0] instr,
  output [3:0] out_14,
  output [3:0] out_15,
  output [3:0] out_16
);

  wire clock_1_out;

  Register #(.width(4)) PCreg (.D(out_14), .en(in_10), .clk(clock_1_out), .Q(out_16), .clr(in_12));
  Clock clock_1 (.out(clock_1_out));
  Multiplexer #(.select(4), .width(8)) multiplexer_1 (
    .in0(in_1), .in1(in_2), .in2(in_3), .in3(in_4), .in4(in_5), .in5(in_6), .in6(in_7), .in7(in_8),
    .in8(unused), .in9(unused), .in10(unused), .in11(unused), .in12(unused), .in13(unused), .in14(unused),
    .in15(unused), .out(instr), .sel(out_16));
  // NoConnect on instr[0]
  // NoConnect on instr[1]
  // NoConnect on instr[7]
  Adder #(.width(4)) adder_1 (.a(out_16), .b(in_11), .out(out_15));  // open: cin, cout
  Multiplexer #(.width(4)) multiplexer_2 (.in0(out_15), .in1(instr[5:2]), .out(out_14), .sel(instr[6]));

  // Notes on the sheet:
  //   bner0 addr
endmodule
