// Logisim project SRlatch.circ as structural Verilog: 1 circuit, main circuit main
module main (
  input  R1,
  input  in_2,
  input  in_3,
  input  S1,
  input  in_5,
  input  in_6,
  input  R,
  input  in_8,
  input  S,
  input  in_10,
  output Q,
  output out_12,
  output Q0,
  output out_14,
  output Q1,
  output out_16,
  output Q00,
  output out_18
);

  wire and_1_out, and_2_out;

  and and_1 (and_1_out, R1, in_2, S1);
  nand nand_1 (Q1, R, Q00);
  nand nand_2 (Q00, Q1, S);
  nand nand_3 (Q, and_1_out, Q0);
  nand nand_4 (Q0, Q, and_1_out);
  and and_2 (and_2_out, in_3, in_5, in_6);
  nor nor_1 (out_12, and_2_out, out_14);
  nor nor_2 (out_14, out_12, and_2_out);
  nor nor_3 (out_16, in_8, out_18);
  nor nor_4 (out_18, out_16, in_10);
endmodule
