// Logisim project dflipfloptrigger.circ as structural Verilog: 1 circuit, main circuit main
module main (
  input  e,
  output out_2
);

  wire and_1_out, d_ff_1_qn, not_1_out;

  not not_1 (not_1_out, e);
  and and_1 (and_1_out, not_1_out, e);
  D_Flip_Flop d_ff_1 (.D(d_ff_1_qn), .clk(and_1_out), .Q(out_2), .Qn(d_ff_1_qn));  // open: preset, reset
endmodule
