// Logisim project orgate.circ as structural Verilog: 1 circuit, main circuit main
module main (
  input  in_1,
  input  in_2,
  input  in_3,
  output out_4
);

  wire transistor_1_out, transistor_2_out;

  Transistor #(.\type ("n")) transistor_1 (.in(in_3), .out(transistor_1_out), .gate(in_1));
  Transistor transistor_2 (.in(1'b1), .out(transistor_2_out), .gate(in_1));
  Transistor transistor_3 (.in(transistor_2_out), .out(in_3), .gate(in_2));
  Transistor #(.\type ("n")) transistor_4 (.in(in_3), .out(transistor_1_out), .gate(in_2));

  assign out_4 = in_3;
  // also tied to GND on the sheet: transistor_1_out
endmodule
