// Logisim project xor.circ as structural Verilog: 1 circuit, main circuit main
module main (
  input  x,
  input  why,
  output o
);

  wire aND1_out, aND2_out, not_1_out, not_2_out;

  not not_1 (not_1_out, why);
  not not_2 (not_2_out, x);
  and aND1 (aND1_out, x, not_1_out);
  and aND2 (aND2_out, not_2_out, why);
  or OR1 (o, aND1_out, aND2_out);

  // Notes on the sheet:
  //   NOT1
  //   NOT2
  //   HOLY-LOGISIM
  //   XOR
endmodule
