// Logisim project sCPU_add.circ as structural Verilog: 1 circuit, main circuit main
module main (
  input  [7:0] in_1,
  input  [7:0] in_2,
  input  [7:0] in_3,
  input  [7:0] in_4,
  input  [7:0] in_5,
  input  [7:0] in_6,
  input  in_7,
  input  in_8,
  input  [7:0] in_9,
  input  en,
  input  rst,
  output [7:0] r0val,
  output [7:0] instr,
  output [7:0] r1val,
  output [7:0] out_15,
  output [7:0] out_16,
  output [7:0] out_17,
  output [7:0] r2val,
  output [7:0] r3val
);

  wire and_1_out, and_2_out, and_3_out, and_4_out, clock_1_out, decoder_1_out0, decoder_1_out2,
       decoder_2_out0, decoder_2_out1, decoder_2_out2, decoder_2_out3, or_1_out;
  wire [2:0] counter_1_q;
  wire [7:0] bit_extender_1_out, multiplexer_2_out;

  Clock clock_1 (.out(clock_1_out));
  Counter #(.max('h7), .width(3)) counter_1 (
    .clr(in_8), .up(in_7), .count(in_7), .clk(clock_1_out), .D(counter_1_q), .Q(counter_1_q));  // open: load, carry
  Multiplexer #(.select(3), .width(8)) multiplexer_1 (
    .in0(in_1), .in1(in_2), .in2(in_3), .in3(in_4), .in4(in_5), .in5(in_6), .in6(in_9), .in7(in_9),
    .out(instr), .sel(counter_1_q));
  Decoder #(.select(2)) decoder_1 (
    .out0(decoder_1_out0), .out2(decoder_1_out2), .sel(instr[7:6]));  // open: out1, out3, en
  assign bit_extender_1_out = {{4{1'b0}}, instr[3:0]};  // Bit_Extender bit_extender_1
  or or_1 (or_1_out, ~decoder_1_out0, decoder_1_out2);  // OR_Gate
  Multiplexer #(.width(8)) multiplexer_2 (
    .in0(out_16), .in1(bit_extender_1_out), .out(multiplexer_2_out), .sel(or_1_out));
  Decoder #(.select(2)) decoder_2 (
    .out0(decoder_2_out0), .out1(decoder_2_out1), .out2(decoder_2_out2), .out3(decoder_2_out3),
    .sel(instr[5:4]));  // open: en
  Register r0 (.D(multiplexer_2_out), .en(and_1_out), .clk(clock_1_out), .Q(r0val), .clr(rst));
  and and_1 (and_1_out, decoder_2_out0, en);
  Register r1 (.D(multiplexer_2_out), .en(and_2_out), .clk(clock_1_out), .Q(r1val), .clr(rst));
  and and_2 (and_2_out, decoder_2_out1, en);
  Register r2 (.D(multiplexer_2_out), .en(and_3_out), .clk(clock_1_out), .Q(r2val), .clr(rst));
  and and_3 (and_3_out, decoder_2_out2, en);
  Register r3 (.D(multiplexer_2_out), .en(and_4_out), .clk(clock_1_out), .Q(r3val), .clr(rst));
  and and_4 (and_4_out, decoder_2_out3, en);
  Multiplexer #(.select(2), .width(8)) multiplexer_3 (
    .in0(r0val), .in1(r1val), .in2(r2val), .in3(r3val), .out(out_15), .sel(instr[1:0]));
  Multiplexer #(.select(2), .width(8)) multiplexer_4 (
    .in0(r0val), .in1(r1val), .in2(r2val), .in3(r3val), .out(out_17), .sel(instr[3:2]));
  Adder adder_1 (.a(out_15), .b(out_17), .out(out_16));  // open: cin, cout
endmodule
