// Logisim project sCPU_bner0_instr.circ as structural Verilog: 1 circuit, main circuit main
module main (
  input  [7:0] in_1,
  input  [7:0] in_2,
  input  [7:0] in_3,
  input  [7:0] in_4,
  input  [7:0] in_5,
  input  [7:0] in_6,
  input  [7:0] in_7,
  input  [7:0] in_8,
  input  in_9,
  input  in_10,
  input  en,
  input  rst,
  output [7:0] r0val,
  output [7:0] instr,
  output [7:0] r1val,
  output [7:0] out_16,
  output [7:0] out_17,
  output [7:0] out_18,
  output [7:0] r2val,
  output [7:0] r3val
);

  wire and_1_out, and_2_out, and_3_out, and_4_out, and_5_out, clock_1_out, comparator_1_eq, decoder_1_out0,
       decoder_1_out1, decoder_1_out2, decoder_1_out3;
  wire [2:0] counter_1_q, multiplexer_2_out;
  wire [7:0] bit_extender_1_out, multiplexer_3_out;

  Clock clock_1 (.out(clock_1_out));
  and and_1 (and_1_out, comparator_1_eq, in_9);
  Counter #(.max('h7), .width(3)) counter_1 (
    .clr(in_10), .up(and_1_out), .count(and_1_out), .clk(clock_1_out), .D(counter_1_q), .Q(counter_1_q));  // open: load, carry
  Multiplexer #(.select(3), .width(8)) multiplexer_1 (
    .in0(in_1), .in1(in_2), .in2(in_3), .in3(in_4), .in4(in_5), .in5(in_6), .in6(in_7), .in7(in_8),
    .out(instr), .sel(multiplexer_2_out));
  Multiplexer #(.width(3)) multiplexer_2 (
    .in0(instr[4:2]), .in1(counter_1_q), .out(multiplexer_2_out), .sel(comparator_1_eq));
  assign bit_extender_1_out = {{4{1'b0}}, instr[3:0]};  // Bit_Extender bit_extender_1
  Multiplexer #(.select(2), .width(8)) multiplexer_3 (
    .in0(out_17), .in2(bit_extender_1_out), .out(multiplexer_3_out), .sel(instr[7:6]));  // open: in1, in3
  Decoder #(.select(2)) decoder_1 (
    .out0(decoder_1_out0), .out1(decoder_1_out1), .out2(decoder_1_out2), .out3(decoder_1_out3),
    .sel(instr[5:4]));  // open: en
  Register r0 (.D(multiplexer_3_out), .en(and_2_out), .clk(clock_1_out), .Q(r0val), .clr(rst));
  and and_2 (and_2_out, decoder_1_out0, en);
  Register r1 (.D(multiplexer_3_out), .en(and_3_out), .clk(clock_1_out), .Q(r1val), .clr(rst));
  and and_3 (and_3_out, decoder_1_out1, en);
  Register r2 (.D(multiplexer_3_out), .en(and_4_out), .clk(clock_1_out), .Q(r2val), .clr(rst));
  and and_4 (and_4_out, decoder_1_out2, en);
  Register r3 (.D(multiplexer_3_out), .en(and_5_out), .clk(clock_1_out), .Q(r3val), .clr(rst));
  and and_5 (and_5_out, decoder_1_out3, en);
  Multiplexer #(.select(2), .width(8)) multiplexer_4 (
    .in0(r0val), .in1(r1val), .in2(r2val), .in3(r3val), .out(out_16), .sel(instr[1:0]));
  Multiplexer #(.select(2), .width(8)) multiplexer_5 (
    .in0(r0val), .in1(r1val), .in2(r2val), .in3(r3val), .out(out_18), .sel(instr[3:2]));
  Comparator comparator_1 (.a(r0val), .b(out_16), .eq(comparator_1_eq));  // open: gt, lt
  Adder adder_1 (.a(out_16), .b(out_18), .out(out_17));  // open: cin, cout
endmodule
