// Logisim project sCPU_io_instr.circ as structural Verilog: 1 circuit, main circuit main
module main (
  input  [7:0] in_1,
  input  [7:0] in_2,
  input  [7:0] in_3,
  input  [7:0] in_4,
  input  [7:0] in_5,
  input  [7:0] in_6,
  input  [7:0] in_7,
  input  [7:0] in_8,
  input  [7:0] in_9,
  input  [7:0] in_10,
  input  in_11,
  input  rst,
  input  en,
  input  [2:0] in_14,
  input  [7:0] in_15,
  input  [3:0] in_16
);

  wire and_1_out, and_2_out, and_3_out, and_4_out, and_5_out, and_6_out, and_7_out, and_8_out, and_9_out,
       and_10_out, clock_1_out, comparator_1_eq, decoder_1_out0, decoder_1_out1, decoder_2_out0,
       decoder_2_out1, decoder_2_out2, decoder_2_out3, or_1_out;
  wire [1:0] demultiplexer_1_out0, demultiplexer_1_out1, demultiplexer_1_out2, demultiplexer_1_out3,
       multiplexer_1_out_2, multiplexer_1_out_3, multiplexer_1_out_4, multiplexer_4_out;
  wire [1:1] multiplexer_1_out;
  wire [2:0] demultiplexer_3_out0, demultiplexer_3_out1, multiplexer_7_out;
  wire [2:2] multiplexer_1_out_5;
  wire [7:0] adder_1_out, adder_2_out, adder_3_out, bit_extender_1_out, bit_extender_2_out, counter_1_q,
       demultiplexer_2_out0, multiplexer_2_out, multiplexer_3_out, multiplexer_5_out, multiplexer_6_out,
       multiplexer_8_out, r0_q, r1_q, r2_q, r3_q, register_1_q;

  Clock clock_1 (.out(clock_1_out));
  Decoder decoder_1 (.out0(decoder_1_out0), .out1(decoder_1_out1), .sel(and_1_out));  // open: en
  and and_1 (and_1_out, ~comparator_1_eq, and_2_out);  // AND_Gate
  Counter counter_1 (
    .clr(in_11), .load(decoder_1_out1), .up(decoder_1_out0), .count(decoder_1_out0), .clk(clock_1_out),
    .D(adder_1_out), .Q(counter_1_q));  // open: carry
  // Probe on counter_1_q[3:0]
  // Probe on {multiplexer_1_out_3, multiplexer_1_out_2, multiplexer_1_out[1], multiplexer_1_out_5[2], multiplexer_1_out_4}
  assign bit_extender_1_out = {{4{multiplexer_1_out_2[1]}}, {multiplexer_1_out_2, multiplexer_1_out[1], multiplexer_1_out_5[2]}};  // Bit_Extender bit_extender_1
  assign bit_extender_2_out = {{4{in_16[3]}}, in_16};  // Bit_Extender bit_extender_2
  Multiplexer #(.select(4), .width(8)) multiplexer_1 (
    .in0(in_1), .in1(in_2), .in2(in_3), .in3(in_4), .in4(in_5), .in5(in_6), .in6(in_7), .in7(in_8),
    .in8(in_9), .in9(in_9), .in10(in_9), .in11(in_9), .in12(in_9), .in13(in_9), .in14(in_9), .in15(in_9),
    .out({multiplexer_1_out_3, multiplexer_1_out_2, multiplexer_1_out[1], multiplexer_1_out_5[2], multiplexer_1_out_4}),
    .sel(counter_1_q[3:0]));
  Adder adder_1 (.a(counter_1_q), .b(bit_extender_1_out), .out(adder_1_out));  // open: cin, cout
  // Probe on adder_1_out
  // Probe on adder_2_out
  Adder adder_2 (.a(in_15), .b(bit_extender_2_out), .out(adder_2_out));  // open: cin, cout
  // Probe on adder_3_out
  // Probe on multiplexer_2_out
  Multiplexer #(.width(8)) multiplexer_2 (
    .in0({demultiplexer_1_out3, demultiplexer_1_out2, demultiplexer_1_out1, demultiplexer_1_out0}),
    .in1(multiplexer_8_out), .out(multiplexer_2_out), .sel(and_4_out));
  Demultiplexer #(.select(2), .width(2)) demultiplexer_1 (
    .out0(demultiplexer_1_out0), .out1(demultiplexer_1_out1), .out2(demultiplexer_1_out2),
    .out3(demultiplexer_1_out3), .in(multiplexer_1_out_4),
    .sel({multiplexer_1_out[1], multiplexer_1_out_5[2]}));
  // Probe on multiplexer_1_out_2
  and and_2 (and_2_out, multiplexer_1_out_3[1], multiplexer_1_out_3[0]);
  and and_3 (and_3_out, and_5_out, multiplexer_1_out[1]);
  // Probe on {multiplexer_1_out_2, multiplexer_1_out[1], multiplexer_1_out_5[2]}
  Multiplexer #(.select(2), .width(8)) multiplexer_3 (
    .in0(adder_3_out), .in1(multiplexer_2_out), .in2(multiplexer_2_out), .out(multiplexer_3_out),
    .sel(multiplexer_1_out_3));  // open: in3
  and and_4 (and_4_out, ~multiplexer_1_out[1], and_5_out);  // AND_Gate
  and and_5 (and_5_out, ~multiplexer_1_out_3[1], multiplexer_1_out_3[0]);  // AND_Gate
  Decoder #(.select(2)) decoder_2 (
    .out0(decoder_2_out0), .out1(decoder_2_out1), .out2(decoder_2_out2), .out3(decoder_2_out3),
    .sel(multiplexer_1_out_2));  // open: en
  or or_1 (or_1_out, ~and_2_out, and_3_out);  // OR_Gate
  and and_6 (and_6_out, or_1_out, en);
  // Probe on multiplexer_3_out
  Register r0 (.D(multiplexer_3_out), .en(and_7_out), .clk(clock_1_out), .Q(r0_q), .clr(rst));
  and and_7 (and_7_out, decoder_2_out0, and_6_out);
  Register r1 (.D(multiplexer_3_out), .en(and_8_out), .clk(clock_1_out), .Q(r1_q), .clr(rst));
  and and_8 (and_8_out, decoder_2_out1, and_6_out);
  Register r2 (.D(multiplexer_3_out), .en(and_9_out), .clk(clock_1_out), .Q(r2_q), .clr(rst));
  and and_9 (and_9_out, decoder_2_out2, and_6_out);
  Register r3 (.D(multiplexer_3_out), .en(and_10_out), .clk(clock_1_out), .Q(r3_q), .clr(rst));
  and and_10 (and_10_out, decoder_2_out3, and_6_out);
  // Probe on r0_q
  // Probe on r1_q
  Multiplexer #(.select(2), .width(2)) multiplexer_4 (
    .in0(multiplexer_1_out_4), .in1(multiplexer_1_out_2), .in2(multiplexer_1_out_4),
    .in3(multiplexer_1_out_4), .out(multiplexer_4_out), .sel(multiplexer_1_out_3));
  // Probe on r2_q
  // Probe on r3_q
  Multiplexer #(.select(2), .width(8)) multiplexer_5 (
    .in0(r0_q), .in1(r1_q), .in2(r2_q), .in3(r3_q), .out(multiplexer_5_out), .sel(multiplexer_4_out));
  // Probe on multiplexer_5_out
  // Probe on multiplexer_4_out
  // Probe on multiplexer_6_out
  Multiplexer #(.select(2), .width(8)) multiplexer_6 (
    .in0(r0_q), .in1(r1_q), .in2(r2_q), .in3(r3_q), .out(multiplexer_6_out),
    .sel({multiplexer_1_out[1], multiplexer_1_out_5[2]}));
  // Probe on {multiplexer_1_out[1], multiplexer_1_out_5[2]}
  Register #(.trigger("falling")) register_1 (.D(r2_q), .en(and_5_out), .clk(clock_1_out), .Q(register_1_q), .clr(rst));
  Comparator comparator_1 (.a(r0_q), .b(multiplexer_5_out), .eq(comparator_1_eq));  // open: gt, lt
  Demultiplexer #(.select(3), .width(8)) demultiplexer_2 (
    .out0(demultiplexer_2_out0), .in(register_1_q), .sel(demultiplexer_3_out1));  // open: out1, out2, out3, out4, out5, out6, out7
  Adder adder_3 (.a(multiplexer_5_out), .b(multiplexer_6_out), .out(adder_3_out));  // open: cin, cout
  Demultiplexer #(.width(3)) demultiplexer_3 (
    .out0(demultiplexer_3_out0), .out1(demultiplexer_3_out1), .in(multiplexer_7_out),
    .sel(multiplexer_1_out[1]));
  Multiplexer #(.width(3)) multiplexer_7 (
    .in0(in_14), .in1({multiplexer_1_out_5[2], multiplexer_1_out_4}), .out(multiplexer_7_out), .sel(and_5_out));
  // Probe on register_1_q
  // LedBar #(.inputtype("row")) ledbar_1: pin names not known; wires that end beside it: demultiplexer_2_out0
  Multiplexer #(.select(3), .width(8)) multiplexer_8 (
    .in0(in_10), .out(multiplexer_8_out), .sel(demultiplexer_3_out0));  // open: in1, in2, in3, in4, in5, in6, in7
endmodule
