// Logisim project sCPU_li.circ as structural Verilog: 1 circuit, main circuit main
module main (
  input  [7:0] in_1,
  input  [7:0] in_2,
  input  [7:0] in_3,
  input  [7:0] in_4,
  input  in_5,
  input  in_6,
  input  en,
  input  rst,
  output [7:0] r0val,
  output [7:0] instr,
  output [7:0] r1val,
  output [7:0] r2val,
  output [7:0] r3val
);

  wire and_1_out, and_2_out, and_3_out, and_4_out, clock_1_out, decoder_1_out0, decoder_1_out1,
       decoder_1_out2, decoder_1_out3;
  wire [1:0] counter_1_q;
  wire [7:0] bit_extender_1_out;

  Clock clock_1 (.out(clock_1_out));
  Counter #(.max('h3), .width(2)) counter_1 (
    .clr(in_6), .up(in_5), .count(in_5), .clk(clock_1_out), .D(counter_1_q), .Q(counter_1_q));  // open: load, carry
  Multiplexer #(.select(2), .width(8)) multiplexer_1 (
    .in0(in_1), .in1(in_2), .in2(in_3), .in3(in_4), .out(instr), .sel(counter_1_q));
  assign bit_extender_1_out = {{4{1'b0}}, instr[3:0]};  // Bit_Extender bit_extender_1
  Decoder #(.select(2)) decoder_1 (
    .out0(decoder_1_out0), .out1(decoder_1_out1), .out2(decoder_1_out2), .out3(decoder_1_out3),
    .sel(instr[5:4]));  // open: en
  Register r0 (.D(bit_extender_1_out), .en(and_1_out), .clk(clock_1_out), .Q(r0val), .clr(rst));
  and and_1 (and_1_out, decoder_1_out0, en);
  Register r1 (.D(bit_extender_1_out), .en(and_2_out), .clk(clock_1_out), .Q(r1val), .clr(rst));
  and and_2 (and_2_out, decoder_1_out1, en);
  Register r2 (.D(bit_extender_1_out), .en(and_3_out), .clk(clock_1_out), .Q(r2val), .clr(rst));
  and and_3 (and_3_out, decoder_1_out2, en);
  Register r3 (.D(bit_extender_1_out), .en(and_4_out), .clk(clock_1_out), .Q(r3val), .clr(rst));
  and and_4 (and_4_out, decoder_1_out3, en);

  // Notes on the sheet:
  //   addr
endmodule
