// Logisim project sCPU_libner0_upd.circ as structural Verilog: 1 circuit, main circuit main
module main (
  input  [7:0] in_1,
  input  [7:0] in_2,
  input  [7:0] in_3,
  input  [7:0] in_4,
  input  [7:0] in_5,
  input  [7:0] in_6,
  input  [7:0] in_7,
  input  [7:0] in_8,
  input  [7:0] in_9,
  input  [7:0] in_10,
  input  in_11,
  input  en,
  input  rst,
  input  [7:0] in_14,
  input  [3:0] in_15
);

  wire and_1_out, and_2_out, and_3_out, and_4_out, and_5_out, and_6_out, and_7_out, clock_1_out,
       comparator_1_eq, decoder_1_out0, decoder_1_out1, decoder_2_out0, decoder_2_out1, decoder_2_out2,
       decoder_2_out3;
  wire [1:0] demultiplexer_1_out0, demultiplexer_1_out1, demultiplexer_1_out2, demultiplexer_1_out3,
       multiplexer_1_out, multiplexer_1_out_2, multiplexer_1_out_3, multiplexer_1_out_4;
  wire [7:0] adder_1_out, adder_2_out, adder_3_out, bit_extender_1_out, bit_extender_2_out, counter_1_q,
       multiplexer_2_out, multiplexer_3_out, multiplexer_4_out, r0_q, r1_q, r2_q, r3_q;

  Clock clock_1 (.out(clock_1_out));
  Decoder decoder_1 (.out0(decoder_1_out0), .out1(decoder_1_out1), .sel(and_1_out));  // open: en
  and and_1 (and_1_out, ~comparator_1_eq, and_2_out);  // AND_Gate
  Counter counter_1 (
    .clr(in_11), .load(decoder_1_out1), .up(decoder_1_out0), .count(decoder_1_out0), .clk(clock_1_out),
    .D(adder_2_out), .Q(counter_1_q));  // open: carry
  // Probe on counter_1_q[3:0]
  assign bit_extender_1_out = {{4{in_15[3]}}, in_15};  // Bit_Extender bit_extender_1
  // Probe on {multiplexer_1_out_4, multiplexer_1_out_2, multiplexer_1_out, multiplexer_1_out_3}
  assign bit_extender_2_out = {{4{multiplexer_1_out_2[1]}}, {multiplexer_1_out_2, multiplexer_1_out}};  // Bit_Extender bit_extender_2
  Adder adder_1 (.a(in_14), .b(bit_extender_1_out), .out(adder_1_out));  // open: cin, cout
  Multiplexer #(.select(4), .width(8)) multiplexer_1 (
    .in0(in_1), .in1(in_2), .in2(in_3), .in3(in_4), .in4(in_5), .in5(in_6), .in6(in_7), .in7(in_8),
    .in8(in_9), .in9(in_10),
    .out({multiplexer_1_out_4, multiplexer_1_out_2, multiplexer_1_out, multiplexer_1_out_3}),
    .sel(counter_1_q[3:0]));  // open: in10, in11, in12, in13, in14, in15
  Adder adder_2 (.a(counter_1_q), .b(bit_extender_2_out), .out(adder_2_out));  // open: cin, cout
  // Probe on adder_2_out
  // Probe on adder_1_out
  // Probe on adder_3_out
  // Probe on {demultiplexer_1_out3, demultiplexer_1_out2, demultiplexer_1_out1, demultiplexer_1_out0}
  Demultiplexer #(.select(2), .width(2)) demultiplexer_1 (
    .out0(demultiplexer_1_out0), .out1(demultiplexer_1_out1), .out2(demultiplexer_1_out2),
    .out3(demultiplexer_1_out3), .in(multiplexer_1_out_3), .sel(multiplexer_1_out));
  // Probe on multiplexer_1_out_2
  and and_2 (and_2_out, multiplexer_1_out_4[1], multiplexer_1_out_4[0]);
  // Probe on {multiplexer_1_out_2, multiplexer_1_out}
  Multiplexer #(.select(2), .width(8)) multiplexer_2 (
    .in0(adder_3_out),
    .in2({demultiplexer_1_out3, demultiplexer_1_out2, demultiplexer_1_out1, demultiplexer_1_out0}),
    .out(multiplexer_2_out), .sel(multiplexer_1_out_4));  // open: in1, in3
  Decoder #(.select(2)) decoder_2 (
    .out0(decoder_2_out0), .out1(decoder_2_out1), .out2(decoder_2_out2), .out3(decoder_2_out3),
    .sel(multiplexer_1_out_2));  // open: en
  and and_3 (and_3_out, ~and_2_out, en);  // AND_Gate
  Register r0 (.D(multiplexer_2_out), .en(and_4_out), .clk(clock_1_out), .Q(r0_q), .clr(rst));
  and and_4 (and_4_out, decoder_2_out0, and_3_out);
  Register r1 (.D(multiplexer_2_out), .en(and_5_out), .clk(clock_1_out), .Q(r1_q), .clr(rst));
  and and_5 (and_5_out, decoder_2_out1, and_3_out);
  Register r2 (.D(multiplexer_2_out), .en(and_6_out), .clk(clock_1_out), .Q(r2_q), .clr(rst));
  and and_6 (and_6_out, decoder_2_out2, and_3_out);
  Register r3 (.D(multiplexer_2_out), .en(and_7_out), .clk(clock_1_out), .Q(r3_q), .clr(rst));
  and and_7 (and_7_out, decoder_2_out3, and_3_out);
  // Probe on r0_q
  // Probe on r1_q
  // Probe on r2_q
  // Probe on r3_q
  // Probe on multiplexer_3_out
  Multiplexer #(.select(2), .width(8)) multiplexer_3 (
    .in0(r0_q), .in1(r1_q), .in2(r2_q), .in3(r3_q), .out(multiplexer_3_out), .sel(multiplexer_1_out_3));
  // Probe on multiplexer_4_out
  Multiplexer #(.select(2), .width(8)) multiplexer_4 (
    .in0(r0_q), .in1(r1_q), .in2(r2_q), .in3(r3_q), .out(multiplexer_4_out), .sel(multiplexer_1_out));
  Comparator comparator_1 (.a(r0_q), .b(multiplexer_3_out), .eq(comparator_1_eq));  // open: gt, lt
  Adder adder_3 (.a(multiplexer_3_out), .b(multiplexer_4_out), .out(adder_3_out));  // open: cin, cout
endmodule
