// Logisim project wip_7segdigitlighter.circ as structural Verilog: 1 circuit, main circuit main
module main (
);

  wire dipswitch_1_p1, dipswitch_1_p2, dipswitch_1_p3, dipswitch_1_p4, dipswitch_1_p5, dipswitch_1_p6,
       dipswitch_1_p7;

  Button button_1 ();  // open: out
  _7_Segment_Display u_7_segment_display_1 (
    .g(dipswitch_1_p7), .f(dipswitch_1_p6), .a(dipswitch_1_p5), .b(dipswitch_1_p4), .e(dipswitch_1_p3),
    .d(dipswitch_1_p2), .c(dipswitch_1_p1));  // open: dp
  LED led_1 ();  // open: in
  // DipSwitch #(.number(7)) dipswitch_1: pin names not known; wires that end beside it: dipswitch_1_p1, dipswitch_1_p2, dipswitch_1_p3, dipswitch_1_p4, dipswitch_1_p5, dipswitch_1_p6, dipswitch_1_p7
endmodule
